// Logisim project main.circ as structural Verilog: 1 circuit, main circuit Game
module Game (
);

  wire and_1_out, and_2_out, and_3_out, and_4_out, and_5_out, Awaiting_user, button_driver_1_p4,
       button_driver_2_p1, button_driver_2_p2, button_driver_3_p2, button_driver_4_p2, button_driver_5_p2,
       button_driver_6_p2, button_register_1_p2, button_register_1_p3, button_register_1_p4,
       button_register_1_p5, button_register_1_p6, button_register_2_p4, button_register_13_p3,
       button_register_13_p4, button_register_13_p5, button_register_13_p6, button_register_13_p7, C,
       Calculating_machine, Calculating_user, cdm_8_mark5_1_p2, Checking_rules, Clock, Data, decoder_2_out0,
       decoder_2_out1, decoder_3_out0, decoder_3_out1, decoder_3_out2, decoder_3_out3, decoder_4_out2,
       decoder_4_out3, Game_starts, Gamepad, gamepad_address_manager_1_p3, H, human_node_6_p2,
       human_node_6_p3, human_node_6_p4, human_node_6_p5, human_node_6_p6, human_node_7_p3, Instructions,
       is_equal_8_bits_1_p3, is_equal_8_bits_2_p3, is_equal_8_bits_3_p3, L, Machine_thinks, Memory,
       not_1_out, not_2_out, not_3_out, or_1_out, R, R___W, ram_address_manager_1_p4, W_out,
       win_lose_draw_1_p3;
  wire [1:0] bit_extender_2_out, register_1_q;
  wire [3:0] Button, button_driver_1_p3, button_register_1_p1, button_register_3_p1, button_register_5_p1,
       button_register_6_p2, button_register_7_p1, button_register_8_p2, button_register_9_p1,
       button_register_11_p1, button_register_12_p2, button_register_13_p1, button_register_14_p1,
       computer_node_1_p2, computer_node_2_p6, computer_node_3_p1, computer_node_4_p1, computer_node_5_p1,
       computer_node_6_p1, computer_node_7_p1, human_node_1_p1, human_node_1_p2, human_node_2_p1,
       human_node_2_p2, human_node_3_p1, human_node_4_p1, human_node_5_p1, human_node_5_p2, human_node_6_p1,
       ram_address_manager_1_p3, win_lose_draw_2_p5;
  wire [7:0] Address_Bus, bit_extender_1_out, cdm_8_mark5_1_p6, cdm_8_mark5_1_p7, controlled_buffer_1_out,
       G_In, G_Out, is_equal_8_bits_3_p1;

  // RAM_Address_Manager ram_address_manager_1: pin names not known; wires that end beside it: Address_Bus, Data, ram_address_manager_1_p3, ram_address_manager_1_p4
  // Is_Equal__8_bits is_equal_8_bits_1: pin names not known; wires that end beside it: Address_Bus, 8'hf0, is_equal_8_bits_1_p3
  // Is_Equal__8_bits is_equal_8_bits_2: pin names not known; wires that end beside it: Address_Bus, 8'hf8, is_equal_8_bits_2_p3
  // CdM_8_mark5 cdm_8_mark5_1: pin names not known; wires that end beside it: Clock, cdm_8_mark5_1_p2, Memory, R___W, Address_Bus, cdm_8_mark5_1_p6, cdm_8_mark5_1_p7
  assign bit_extender_1_out = {{4{1'b1}}, Button};  // Bit_Extender bit_extender_1
  and and_1 (and_1_out, is_equal_8_bits_2_p3, Data);
  Decoder #(.disabled(0)) decoder_1 (.out0(Instructions), .out1(Data), .sel(cdm_8_mark5_1_p2), .en(Memory));
  assign controlled_buffer_1_out = not_1_out ? cdm_8_mark5_1_p6 : 8'bz;  // Controlled_Buffer controlled_buffer_1
  not not_1 (not_1_out, R___W);
  assign cdm_8_mark5_1_p7 = R___W ? controlled_buffer_1_out : 8'bz;  // Controlled_Buffer controlled_buffer_2
  ROM rom_1 (.addr(Address_Bus), .data(controlled_buffer_1_out), .sel(decoder_3_out0));
  ROM rom_2 (.addr(Address_Bus), .data(controlled_buffer_1_out), .sel(decoder_3_out1));
  ROM rom_3 (.addr(Address_Bus), .data(controlled_buffer_1_out), .sel(decoder_3_out2));
  ROM rom_4 (.addr(Address_Bus), .data(controlled_buffer_1_out), .sel(decoder_3_out3));
  RAM #(.addrWidth(4)) ram_1 (
    .addr(ram_address_manager_1_p3), .data(controlled_buffer_1_out), .sel(ram_address_manager_1_p4),
    .clk(Clock), .ld(R___W));  // open: clr
  and and_2 (and_2_out, ~R___W, is_equal_8_bits_1_p3, Data);  // AND_Gate
  and and_3 (and_3_out, ~R___W, and_1_out);  // AND_Gate
  and and_4 (and_4_out, R___W, and_1_out);
  assign G_In = decoder_2_out0 ? controlled_buffer_1_out : 8'bz;  // Controlled_Buffer controlled_buffer_3
  Decoder #(.disabled(0)) decoder_2 (.out0(decoder_2_out0), .out1(decoder_2_out1), .sel(R___W), .en(Gamepad));
  assign controlled_buffer_1_out = decoder_2_out1 ? G_Out : 8'bz;  // Controlled_Buffer controlled_buffer_4
  Bit_Extender #(.out_width(2)) bit_extender_2 (.in(controlled_buffer_1_out), .out(bit_extender_2_out));
  assign bit_extender_1_out = and_3_out ? controlled_buffer_1_out : 8'bz;  // Controlled_Buffer controlled_buffer_5
  or or_1 (or_1_out, and_3_out, is_equal_8_bits_3_p3);
  assign controlled_buffer_1_out = and_4_out ? is_equal_8_bits_3_p1 : 8'bz;  // Controlled_Buffer controlled_buffer_6
  Clock clock_1 (.out(Clock));
  Decoder #(.select(2), .disabled(0)) decoder_3 (
    .out0(decoder_3_out0), .out1(decoder_3_out1), .out2(decoder_3_out2), .out3(decoder_3_out3),
    .sel(register_1_q), .en(and_5_out));
  Register #(.width(2)) register_1 (
    .D(bit_extender_2_out), .en(and_2_out), .Q(register_1_q), .clk(Clock));  // open: clr
  Decoder #(.select(2), .disabled(0), .enable("false")) decoder_4 (
    .out0(Game_starts), .out1(Checking_rules), .out2(decoder_4_out2), .out3(decoder_4_out3),
    .sel(register_1_q));
  and and_5 (and_5_out, ~Data, Memory);  // AND_Gate
  // Is_Equal__8_bits is_equal_8_bits_3: pin names not known; wires that end beside it: is_equal_8_bits_3_p1, {8{1'b1}}, is_equal_8_bits_3_p3
  Register #(.trigger("low")) register_2 (
    .D(bit_extender_1_out), .en(or_1_out), .Q(is_equal_8_bits_3_p1), .clk(1'b0));  // open: clr
  assign Calculating_user = not_2_out ? decoder_4_out2 : 1'bz;  // Controlled_Buffer controlled_buffer_7
  assign Calculating_machine = not_2_out ? decoder_4_out3 : 1'bz;  // Controlled_Buffer controlled_buffer_8
  not not_2 (not_2_out, or_1_out);
  and and_6 (Awaiting_user, decoder_4_out2, or_1_out);
  and and_7 (Machine_thinks, or_1_out, decoder_4_out3);
  LED led_1 (.in(C));
  LED led_2 (.in(C));
  LED led_3 (.in(C));
  Pull_Resistor pull_resistor_1 (.node(C));
  // Computer_Node computer_node_1: pin names not known; wires that end beside it: G_Out, computer_node_1_p2
  Hex_Digit_Display hex_digit_display_1 (.value(computer_node_1_p2));  // open: dp
  Hex_Digit_Display hex_digit_display_2 (.value(button_register_1_p1));  // open: dp
  nand W (W_out, ~R___W, Gamepad, Data);  // NAND_Gate
  // Gamepad_Address_Manager gamepad_address_manager_1: pin names not known; wires that end beside it: Address_Bus, Data, gamepad_address_manager_1_p3, Gamepad
  // Button_Register button_register_1: pin names not known; wires that end beside it: button_register_1_p1, button_register_1_p2, button_register_1_p3, button_register_1_p4, button_register_1_p5, button_register_1_p6, computer_node_1_p2, button_register_1_p1
  assign Button = not_3_out ? button_driver_1_p3 : 4'bz;  // Controlled_Buffer controlled_buffer_9
  // Computer_Node computer_node_2: pin names not known; wires that end beside it: button_register_1_p2, button_register_1_p3, button_register_1_p4, button_register_1_p5, button_register_1_p6, computer_node_2_p6
  Hex_Digit_Display hex_digit_display_3 (.value(button_register_3_p1));  // open: dp
  // Win_Lose_Draw win_lose_draw_1: pin names not known; wires that end beside it: C, L, win_lose_draw_1_p3, R
  Hex_Digit_Display hex_digit_display_4 (.value(human_node_1_p1));  // open: dp
  // Button_Register button_register_2: pin names not known; wires that end beside it: G_In, 4'b0000, gamepad_address_manager_1_p3, button_register_2_p4
  // Human_Node human_node_1: pin names not known; wires that end beside it: human_node_1_p1, human_node_1_p2
  // Button_Driver button_driver_1: pin names not known; wires that end beside it: Clock, W_out, button_driver_1_p3, button_driver_1_p4
  Button button_1 (.out(button_driver_1_p4));
  not not_3 (not_3_out, button_driver_2_p1);
  // Button_Register button_register_3: pin names not known; wires that end beside it: button_register_3_p1, win_lose_draw_1_p3
  Hex_Digit_Display hex_digit_display_5 (.value(computer_node_2_p6));  // open: dp
  LED led_4 (.in(Calculating_machine));
  LED led_5 (.in(Calculating_machine));
  LED led_6 (.in(Calculating_machine));
  Hex_Digit_Display hex_digit_display_6 (.value(human_node_1_p2));  // open: dp
  // Button_Register button_register_4: pin names not known; wires that end beside it: button_register_2_p4
  // Button_Driver button_driver_2: pin names not known; wires that end beside it: button_driver_2_p1, button_driver_2_p2
  // Computer_Node computer_node_3: pin names not known; wires that end beside it: computer_node_3_p1
  Hex_Digit_Display hex_digit_display_7 (.value(computer_node_3_p1));  // open: dp
  Hex_Digit_Display hex_digit_display_8 (.value(button_register_5_p1));  // open: dp
  LED led_7 (.in(Machine_thinks));
  LED led_8 (.in(Machine_thinks));
  LED led_9 (.in(Machine_thinks));
  Hex_Digit_Display hex_digit_display_9 (.value(human_node_2_p2));  // open: dp
  Hex_Digit_Display hex_digit_display_10 (.value(human_node_2_p1));  // open: dp
  // Human_Node human_node_2: pin names not known; wires that end beside it: human_node_2_p1, human_node_2_p2
  Button button_2 (.out(button_driver_2_p2));
  // Computer_Node computer_node_4: pin names not known; wires that end beside it: computer_node_4_p1
  // Button_Register button_register_5: pin names not known; wires that end beside it: button_register_5_p1, win_lose_draw_1_p3
  Hex_Digit_Display hex_digit_display_11 (.value(button_register_7_p1));  // open: dp
  Hex_Digit_Display hex_digit_display_12 (.value(computer_node_4_p1));  // open: dp
  LED led_10 (.in(Game_starts));
  LED led_11 (.in(Game_starts));
  Hex_Digit_Display hex_digit_display_13 (.value(button_register_6_p2));  // open: dp
  Hex_Digit_Display hex_digit_display_14 (.value(human_node_3_p1));  // open: dp
  // Button_Register button_register_6: pin names not known; wires that end beside it: button_register_2_p4, button_register_6_p2
  // Human_Node human_node_3: pin names not known; wires that end beside it: human_node_3_p1
  // Button_Driver button_driver_3: pin names not known; wires that end beside it: button_driver_2_p1, button_driver_3_p2
  Button button_3 (.out(button_driver_3_p2));
  // Computer_Node computer_node_5: pin names not known; wires that end beside it: computer_node_5_p1
  // Button_Register button_register_7: pin names not known; wires that end beside it: button_register_7_p1, win_lose_draw_1_p3
  Hex_Digit_Display hex_digit_display_15 (.value(button_register_9_p1));  // open: dp
  LED led_12 (.in(Checking_rules));
  LED led_13 (.in(Game_starts));
  Hex_Digit_Display hex_digit_display_16 (.value(button_register_8_p2));  // open: dp
  // Button_Register button_register_8: pin names not known; wires that end beside it: button_register_2_p4, button_register_8_p2
  // Button_Driver button_driver_4: pin names not known; wires that end beside it: button_driver_2_p1, button_driver_4_p2
  Button button_4 (.out(button_driver_4_p2));
  // Button_Register button_register_9: pin names not known; wires that end beside it: button_register_9_p1, win_lose_draw_1_p3
  Hex_Digit_Display hex_digit_display_17 (.value(computer_node_5_p1));  // open: dp
  LED led_14 (.in(Checking_rules));
  LED led_15 (.in(Checking_rules));
  Hex_Digit_Display hex_digit_display_18 (.value(human_node_4_p1));  // open: dp
  // Button_Register button_register_10: pin names not known; wires that end beside it: button_register_2_p4
  // Human_Node human_node_4: pin names not known; wires that end beside it: human_node_4_p1
  // Button_Driver button_driver_5: pin names not known; wires that end beside it: button_driver_2_p1, button_driver_5_p2
  // Computer_Node computer_node_6: pin names not known; wires that end beside it: computer_node_6_p1
  Hex_Digit_Display hex_digit_display_19 (.value(computer_node_6_p1));  // open: dp
  Hex_Digit_Display hex_digit_display_20 (.value(button_register_11_p1));  // open: dp
  LED led_16 (.in(Awaiting_user));
  LED led_17 (.in(Awaiting_user));
  LED led_18 (.in(Awaiting_user));
  Hex_Digit_Display hex_digit_display_21 (.value(human_node_5_p1));  // open: dp
  Hex_Digit_Display hex_digit_display_22 (.value(human_node_5_p2));  // open: dp
  // Human_Node human_node_5: pin names not known; wires that end beside it: human_node_5_p1, human_node_5_p2
  Button button_5 (.out(button_driver_5_p2));
  // Computer_Node computer_node_7: pin names not known; wires that end beside it: computer_node_7_p1
  // Button_Register button_register_11: pin names not known; wires that end beside it: button_register_11_p1, win_lose_draw_1_p3
  Hex_Digit_Display hex_digit_display_23 (.value(button_register_13_p1));  // open: dp
  LED led_19 (.in(Calculating_user));
  LED led_20 (.in(Calculating_user));
  LED led_21 (.in(Calculating_user));
  Hex_Digit_Display hex_digit_display_24 (.value(button_register_12_p2));  // open: dp
  // Button_Register button_register_12: pin names not known; wires that end beside it: button_register_2_p4, button_register_12_p2
  // Human_Node human_node_6: pin names not known; wires that end beside it: human_node_6_p1, human_node_6_p2, human_node_6_p3, human_node_6_p4, human_node_6_p5, human_node_6_p6
  // Button_Driver button_driver_6: pin names not known; wires that end beside it: button_driver_2_p1, button_driver_6_p2, button_driver_2_p1, 4'b0000
  Button button_6 (.out(button_driver_6_p2));
  // Button_Register button_register_13: pin names not known; wires that end beside it: button_register_13_p1, win_lose_draw_1_p3, button_register_13_p3, button_register_13_p4, button_register_13_p5, button_register_13_p6, button_register_13_p7
  Pull_Resistor #(.pull(1)) pull_resistor_2 (.node(win_lose_draw_1_p3));
  Hex_Digit_Display hex_digit_display_25 (.value(computer_node_7_p1));  // open: dp
  // Win_Lose_Draw win_lose_draw_2: pin names not known; wires that end beside it: L, button_register_2_p4, R, H, win_lose_draw_2_p5
  Pull_Resistor #(.pull(1)) pull_resistor_3 (.node(button_register_2_p4));
  Hex_Digit_Display hex_digit_display_26 (.value(human_node_6_p1));  // open: dp
  Pull_Resistor #(.pull(1)) pull_resistor_4 (.node(button_driver_2_p1));
  Hex_Digit_Display hex_digit_display_27 (.value(win_lose_draw_2_p5));  // open: dp
  // Button_Register button_register_14: pin names not known; wires that end beside it: button_register_14_p1, human_node_6_p2, human_node_6_p3, human_node_6_p4, human_node_6_p5, human_node_6_p6, win_lose_draw_2_p5
  // Human_Node human_node_7: pin names not known; wires that end beside it: button_register_14_p1, button_register_13_p7, human_node_7_p3, button_register_13_p5, button_register_13_p4, button_register_13_p3
  // Increment__4_bits increment_4_bits_1: pin names not known; wires that end beside it: button_register_13_p6, human_node_7_p3
  LED led_22 (.in(H));
  LED led_23 (.in(H));
  Pull_Resistor pull_resistor_5 (.node(H));
  LED led_24 (.in(H));
  Hex_Digit_Display hex_digit_display_28 (.value(button_register_14_p1));  // open: dp

  // Notes on the sheet:
  //   contents of rom_1 (hex, n*v repeats v):
  //   d0 f0 d2 0 d3 0 a1 cd f0 d2 4 d3 0 d0 f1 d1 f7 74 ed 18 a2 8c ee 11 a3 d0 f9 d1 ff 74 ed 24 a2 8c ee
  //   1d a3 d1 2 ee
  //   contents of rom_2 (hex, n*v repeats v):
  //   d0 f0 d2 0 d3 0 a1 d0 e2 b2 d1 f7 79 e0 51 d1 ff 79 e0 51 d1 1 b8 74 e1 51 d0 e1 d1 e2 b2 b7 6b 9b
  //   9b 9b e1 51 b4 3 d2 ff 3b d2 f0 1b be a e1 34 ee 51 d2 e2 b2 d1 0 a1 c b1 8d d2 0 a2 d3 e0 bc d2 2
  //   72 e1 4c d2 f7 ee 4e d2 ff b8 14 a8 d2 0 d0 f9 d1 ff d6 9c d0 f1 d1 f7 d6 9c a e1 63 d4 d2 0 d0 f1
  //   d6 9c a e1 70 d1 3 ee 0 d2 e2 b9 71 e1 7a d1 2 ee 0 d0 f9 d1 ff d2 0 d6 9c a e1 89 d1 2 ee 0 d2 e2
  //   b9 71 e1 93 d1 3 ee 0 d1 5 d3 e0 bc 34 1 ee 0 71 e0 a4 b3 1e 8c ee 9c d7
  //   contents of rom_3 (hex, n*v repeats v):
  //   d0 f0 d2 0 d3 0 a1 d0 f8 d1 ff d2 ff a1 b1 76 e0 e d2 f0 a2 d3 e1 ad b4 d2 0 a6 0 ed 33 8d d2 f8 76
  //   e1 26 8d d2 ff 76 e1 2d d1 f1 b7 8f a7 88 ee 1c d3 e2 ad d3 e0 d2 2 ae d1 1 ee
  //   contents of rom_4 (hex, n*v repeats v):
  //   d0 f0 d2 0 d3 0 a1 d0 f8 d1 ff a1 d0 f9 d2 d d3 ff 73 ea 28 b1 76 eb 1f 36 9 d2 d ee 16 11 77 e1 25
  //   ee 52 8c ee 12 d0 f9 d3 ff 73 ea 41 b1 76 e0 3c 11 b7 f e1 3e b1 5 ed 3e ee 52 8c ee 2a d0 ff 88 d1
  //   f9 71 eb 52 b2 a ed 4f ee 52 88 ee 46 d3 e1 ac 1 d0 f8 d2 f0 a2 b4 d2 0 a6 0 ed 77 d2 ff 76 e1 69 d1
  //   f0 8d d2 f7 76 e1 71 d1 f9 b7 8f a7 88 ee 5f d3 e2 ad d3 e0 d2 3 ae d1 1 ee
  //   Initialization
  //   Referee
  //   Human
  //   Computer
endmodule
